# Fritzing sketch sketch (saved by Fritzing 0.9.3b)
breadboards: 1

parts:
  Part1 = Arduino Uno (Rev3)
  HC-SR04_Sensor_1 = HC-SR04 Ultrasonic Distance Sensor
  J1 = Piezo Speaker
  S1 = Momentary Switch [package=ksa_sealed_tac_switch]
  R1 = Resistor [tolerance=±5% resistance=10k package="2010 [SMD]"]
  LED1 = LED - 5mm [color="Red (633nm)" package="5 mm [THT]"]
  R2 = Resistor [tolerance=±5% resistance=10k package="2010 [SMD]"]

nets:
  N1: Part1.D8, J1.pin2
  N2: Part1.D9_PWM, HC-SR04_Sensor_1.ECHO
  N3: Part1.D10_PWM/SS, HC-SR04_Sensor_1.TRIG
  N4: Part1.D2, S1.1
  N5: Part1.D6_PWM, R2.Pin_0
  5V: Part1.5V, HC-SR04_Sensor_1.VCC, S1.4
  GND: Part1.GND, HC-SR04_Sensor_1.GND, J1.pin1, R1.Pin_1, LED1.cathode
  N6: S1.2, R1.Pin_0
  N7: LED1.anode, R2.Pin_1
